// Logisim project BC1.circ as structural Verilog: 7 circuits, main circuit main
module main (
  input  ON_OFF
);

  wire and_1_out, buffer_1_out, clock_1_out, cpu_1_write_to_memory, io_splitter_1_interrupt,
       io_splitter_1_port_1_data_ready, io_splitter_1_port_2_data_ready, io_splitter_1_port_3_data_ready,
       keyboard_1_avail, not_1_out, not_2_out, undriven_2, undriven_4;
  wire [3:0] cpu_1_io_port;
  wire [6:0] keyboard_1_data;
  wire [7:0] cpu_1_data_out, cpu_1_memory_address, io_splitter_1_data_to_cpu, io_splitter_1_port_1_data_out,
       io_splitter_1_port_2_data_out, io_splitter_1_port_3_data_out, ram_1_data, undriven, undriven_3;
  wire [8:0] cpu_1_instruction_address;
  wire [15:0] frame_buffer_1_out_3, frame_buffer_1_out_4, frame_buffer_1_out_5, frame_buffer_1_out_6,
       frame_buffer_1_out_7, frame_buffer_1_out_8, frame_buffer_1_out_9, frame_buffer_1_out_10,
       frame_buffer_1_out_11, frame_buffer_1_out_12, frame_buffer_1_out_13, frame_buffer_1_out_14,
       frame_buffer_1_out_15, frame_buffer_1_out_16, frame_buffer_1_out_17, frame_buffer_1_out_18, rom_1_data;

  Clock clock_1 (.out(clock_1_out));
  and and_1 (and_1_out, clock_1_out, ON_OFF);
  cpu cpu_1 (
    .clock(and_1_out), .instruction(rom_1_data), .data_in(io_splitter_1_data_to_cpu),
    .memory_data_in(ram_1_data), .instruction_address(cpu_1_instruction_address),
    .write_to_memory(cpu_1_write_to_memory), .io_port(cpu_1_io_port), .data_out(cpu_1_data_out),
    .memory_address(cpu_1_memory_address), .interrupt(io_splitter_1_interrupt));
  not not_1 (not_1_out, and_1_out);
  buf buffer_1 (buffer_1_out, cpu_1_write_to_memory);
  not not_2 (not_2_out, cpu_1_write_to_memory);
  RAM #(.bus("separate")) ram_1 (
    .addr(cpu_1_memory_address), .din(cpu_1_data_out), .data(ram_1_data), .str(buffer_1_out),
    .clk(not_1_out), .ld(not_2_out));  // open: sel, clr
  ROM #(.addrWidth(9), .dataWidth(16)) rom_1 (.addr(cpu_1_instruction_address), .data(rom_1_data));  // open: sel
  io_splitter io_splitter_1 (
    .port(cpu_1_io_port), .clock(and_1_out), .port_1_data_out(io_splitter_1_port_1_data_out),
    .port_1_data_in({1'b0, keyboard_1_data}), .port_1_interrupt_line(keyboard_1_avail),
    .port_1_data_ready(io_splitter_1_port_1_data_ready), .port_2_data_out(io_splitter_1_port_2_data_out),
    .port_2_data_in(undriven), .port_2_interrupt_line(undriven_2),
    .port_2_data_ready(io_splitter_1_port_2_data_ready), .port_3_data_out(io_splitter_1_port_3_data_out),
    .port_3_data_in(undriven_3), .port_3_interrupt_line(undriven_4),
    .port_3_data_ready(io_splitter_1_port_3_data_ready), .interrupt(io_splitter_1_interrupt),
    .data_to_cpu(io_splitter_1_data_to_cpu), .data_out(cpu_1_data_out));
  Keyboard keyboard_1 (
    .clk(io_splitter_1_port_1_data_ready), .avail(keyboard_1_avail), .data(keyboard_1_data));  // open: re, clr
  DotMatrix #(.inputtype("row"), .matrixcols(16), .matrixrows(16)) dotmatrix_1 (
    .row0(frame_buffer_1_out_3), .row1(frame_buffer_1_out_4), .row2(frame_buffer_1_out_5),
    .row3(frame_buffer_1_out_6), .row4(frame_buffer_1_out_7), .row5(frame_buffer_1_out_8),
    .row6(frame_buffer_1_out_9), .row7(frame_buffer_1_out_10), .row8(frame_buffer_1_out_11),
    .row9(frame_buffer_1_out_12), .row10(frame_buffer_1_out_13), .row11(frame_buffer_1_out_14),
    .row12(frame_buffer_1_out_15), .row13(frame_buffer_1_out_16), .row14(frame_buffer_1_out_17),
    .row15(frame_buffer_1_out_18));
  frame_buffer frame_buffer_1 (
    .out_3(frame_buffer_1_out_3), .out_4(frame_buffer_1_out_4), .out_5(frame_buffer_1_out_5),
    .out_6(frame_buffer_1_out_6), .out_7(frame_buffer_1_out_7), .out_8(frame_buffer_1_out_8),
    .out_9(frame_buffer_1_out_9), .out_10(frame_buffer_1_out_10), .out_11(frame_buffer_1_out_11),
    .out_12(frame_buffer_1_out_12), .out_13(frame_buffer_1_out_13), .out_14(frame_buffer_1_out_14),
    .out_15(frame_buffer_1_out_15), .out_16(frame_buffer_1_out_16), .out_17(frame_buffer_1_out_17),
    .out_18(frame_buffer_1_out_18), .data_in(io_splitter_1_port_3_data_out),
    .update(io_splitter_1_port_3_data_ready));
  TTY tty_1 (
    .data(io_splitter_1_port_2_data_out[6:0]), .clk(io_splitter_1_port_2_data_ready),
    .clr(io_splitter_1_port_2_data_out[7]));  // open: we

  // Notes on the sheet:
  //   contents of rom_1 (hex, n*v repeats v):
  //   0 5111 9310 7101 c002 1123 201 302 c004
endmodule

module alu (
  input  [3:0] alu_opcode,
  input  [7:0] A,
  input  cin,
  input  [7:0] B,
  output cout,
  output [7:0] C,
  output A_B,
  output zero
);

  wire decoder_1_out2, decoder_1_out6, decoder_1_out7, decoder_1_out15, not_1_out, not_2_out, or_1_out;
  wire [7:0] adder_1_out, and_1_out, buffer_1_out, buffer_2_out, controlled_buffer_1_out,
       controlled_buffer_2_out, or_2_out, shifter_1_out, xor_1_out;

  Decoder #(.select(4), .disabled(0), .enable("false")) decoder_1 (
    .out2(decoder_1_out2), .out6(decoder_1_out6), .out7(decoder_1_out7), .out15(decoder_1_out15),
    .sel(alu_opcode));  // open: out0, out1, out3, out4, out5, out8, out9, out10, out11, out12, out13, out14
  assign buffer_1_out = A;  // Buffer buffer_1, 8 bits wide
  not not_1 (not_1_out, decoder_1_out7);
  assign controlled_buffer_1_out = not_1_out ? B : 8'bz;  // Controlled_Buffer controlled_buffer_1
  Pull_Resistor pull_resistor_1 (.node(controlled_buffer_1_out));
  or or_1 (or_1_out, decoder_1_out6, decoder_1_out15, decoder_1_out2);
  assign buffer_2_out = buffer_1_out;  // Buffer buffer_2, 8 bits wide
  assign controlled_buffer_2_out = not_2_out ? controlled_buffer_1_out : 8'bz;  // Controlled_Buffer controlled_buffer_2
  not not_2 (not_2_out, or_1_out);
  assign controlled_buffer_2_out = not_2_out ? ~controlled_buffer_1_out : 8'bz;  // Controlled_Inverter controlled_inverter_1
  // Buffer buffer_3 has open pins: in=or_1_out, out=open
  assign and_1_out = buffer_1_out & controlled_buffer_1_out;  // AND_Gate and_1, 8 bits wide
  assign or_2_out = buffer_1_out | controlled_buffer_1_out;  // OR_Gate or_2, 8 bits wide
  assign xor_1_out = buffer_1_out ^ controlled_buffer_1_out;  // XOR_Gate xor_1, 8 bits wide
  Adder adder_1 (.a(buffer_2_out), .b(controlled_buffer_2_out), .out(adder_1_out), .cin(cin), .cout(cout));
  Comparator #(.mode("unsigned")) comparator_1 (
    .a(buffer_1_out), .b(controlled_buffer_1_out), .gt(A_B));  // open: eq, lt
  Shifter shifter_1 (.in(buffer_1_out), .\dist (controlled_buffer_1_out[2:0]), .out(shifter_1_out));
  Multiplexer #(.select(4), .width(8), .disabled(0), .enable("false")) multiplexer_1 (
    .in0(buffer_1_out), .in1(adder_1_out), .in2(adder_1_out), .in3(and_1_out), .in4(or_2_out),
    .in5(xor_1_out), .in6(controlled_buffer_2_out), .in7(adder_1_out), .in14(shifter_1_out),
    .in15(adder_1_out), .out(C), .sel(alu_opcode));  // open: in8, in9, in10, in11, in12, in13
  nor nor_1 (zero, C[7], C[6], C[5], C[4], C[3], C[2], C[1], C[0]);
endmodule

// reg
module register_file (
  input  [3:0] read_A,
  input  [3:0] read_B,
  input  clock,
  input  [7:0] data,
  input  save,
  input  [3:0] save_reg,
  output [7:0] A,
  output [7:0] B
);

  wire decoder_1_out0, decoder_1_out1, decoder_1_out2, decoder_1_out3, decoder_1_out4, decoder_1_out5,
       decoder_1_out6, decoder_1_out7, decoder_1_out8, decoder_1_out9, decoder_1_out10, decoder_1_out11,
       decoder_1_out12, decoder_1_out13, decoder_1_out14, decoder_1_out15, decoder_2_out0, decoder_2_out1,
       decoder_2_out2, decoder_2_out3, decoder_2_out4, decoder_2_out5, decoder_2_out6, decoder_2_out7,
       decoder_2_out8, decoder_2_out9, decoder_2_out10, decoder_2_out11, decoder_2_out12, decoder_2_out13,
       decoder_2_out14, decoder_2_out15, decoder_3_out1, decoder_3_out2, decoder_3_out3, decoder_3_out4,
       decoder_3_out5, decoder_3_out6, decoder_3_out7, decoder_3_out8, decoder_3_out9, decoder_3_out10,
       decoder_3_out11, decoder_3_out12, decoder_3_out13, decoder_3_out14, decoder_3_out15;
  wire [7:0] controlled_buffer_1_out, controlled_buffer_2_out, register_1_q, register_2_q, register_3_q,
       register_4_q, register_5_q, register_6_q, register_7_q, register_8_q, register_9_q, register_10_q,
       register_11_q, register_12_q, register_13_q, register_14_q, register_15_q, register_16_q;

  Decoder #(.select(4), .disabled(0), .enable("false")) decoder_1 (
    .out0(decoder_1_out0), .out1(decoder_1_out1), .out2(decoder_1_out2), .out3(decoder_1_out3),
    .out4(decoder_1_out4), .out5(decoder_1_out5), .out6(decoder_1_out6), .out7(decoder_1_out7),
    .out8(decoder_1_out8), .out9(decoder_1_out9), .out10(decoder_1_out10), .out11(decoder_1_out11),
    .out12(decoder_1_out12), .out13(decoder_1_out13), .out14(decoder_1_out14), .out15(decoder_1_out15),
    .sel(read_A));
  Decoder #(.select(4), .disabled(0), .enable("false")) decoder_2 (
    .out0(decoder_2_out0), .out1(decoder_2_out1), .out2(decoder_2_out2), .out3(decoder_2_out3),
    .out4(decoder_2_out4), .out5(decoder_2_out5), .out6(decoder_2_out6), .out7(decoder_2_out7),
    .out8(decoder_2_out8), .out9(decoder_2_out9), .out10(decoder_2_out10), .out11(decoder_2_out11),
    .out12(decoder_2_out12), .out13(decoder_2_out13), .out14(decoder_2_out14), .out15(decoder_2_out15),
    .sel(read_B));
  Decoder #(.select(4), .disabled(0)) decoder_3 (
    .out1(decoder_3_out1), .out2(decoder_3_out2), .out3(decoder_3_out3), .out4(decoder_3_out4),
    .out5(decoder_3_out5), .out6(decoder_3_out6), .out7(decoder_3_out7), .out8(decoder_3_out8),
    .out9(decoder_3_out9), .out10(decoder_3_out10), .out11(decoder_3_out11), .out12(decoder_3_out12),
    .out13(decoder_3_out13), .out14(decoder_3_out14), .out15(decoder_3_out15), .sel(save_reg), .en(save));  // open: out0
  Register register_1 (.D(data), .Q(register_1_q));  // open: en, clk, clr
  assign controlled_buffer_1_out = decoder_2_out0 ? register_1_q : 8'bz;  // Controlled_Buffer controlled_buffer_1
  assign controlled_buffer_2_out = decoder_1_out0 ? register_1_q : 8'bz;  // Controlled_Buffer controlled_buffer_2
  Register register_2 (.D(data), .Q(register_2_q), .clk(decoder_3_out1));  // open: en, clr
  assign controlled_buffer_2_out = decoder_1_out1 ? register_2_q : 8'bz;  // Controlled_Buffer controlled_buffer_3
  assign controlled_buffer_1_out = decoder_2_out1 ? register_2_q : 8'bz;  // Controlled_Buffer controlled_buffer_4
  Register register_3 (.D(data), .Q(register_3_q), .clk(decoder_3_out2));  // open: en, clr
  Register register_4 (.D(data), .Q(register_4_q), .clk(decoder_3_out3));  // open: en, clr
  assign controlled_buffer_1_out = decoder_2_out3 ? register_4_q : 8'bz;  // Controlled_Buffer controlled_buffer_5
  assign controlled_buffer_2_out = decoder_1_out2 ? register_3_q : 8'bz;  // Controlled_Buffer controlled_buffer_6
  assign controlled_buffer_1_out = decoder_2_out2 ? register_3_q : 8'bz;  // Controlled_Buffer controlled_buffer_7
  Register register_5 (.D(data), .Q(register_5_q), .clk(decoder_3_out4));  // open: en, clr
  assign controlled_buffer_2_out = decoder_1_out4 ? register_5_q : 8'bz;  // Controlled_Buffer controlled_buffer_8
  assign controlled_buffer_2_out = decoder_1_out3 ? register_4_q : 8'bz;  // Controlled_Buffer controlled_buffer_9
  assign controlled_buffer_1_out = decoder_2_out4 ? register_5_q : 8'bz;  // Controlled_Buffer controlled_buffer_10
  Register register_6 (.D(data), .Q(register_6_q), .clk(decoder_3_out5));  // open: en, clr
  assign controlled_buffer_2_out = decoder_1_out5 ? register_6_q : 8'bz;  // Controlled_Buffer controlled_buffer_11
  assign controlled_buffer_1_out = decoder_2_out5 ? register_6_q : 8'bz;  // Controlled_Buffer controlled_buffer_12
  Register register_7 (.D(data), .Q(register_7_q), .clk(decoder_3_out6));  // open: en, clr
  assign controlled_buffer_1_out = decoder_2_out6 ? register_7_q : 8'bz;  // Controlled_Buffer controlled_buffer_13
  assign controlled_buffer_2_out = decoder_1_out6 ? register_7_q : 8'bz;  // Controlled_Buffer controlled_buffer_14
  Register register_8 (.D(data), .Q(register_8_q), .clk(decoder_3_out7));  // open: en, clr
  assign controlled_buffer_1_out = decoder_2_out7 ? register_8_q : 8'bz;  // Controlled_Buffer controlled_buffer_15
  assign controlled_buffer_2_out = decoder_1_out7 ? register_8_q : 8'bz;  // Controlled_Buffer controlled_buffer_16
  Register register_9 (.D(data), .Q(register_9_q), .clk(decoder_3_out8));  // open: en, clr
  assign controlled_buffer_2_out = decoder_1_out8 ? register_9_q : 8'bz;  // Controlled_Buffer controlled_buffer_17
  assign controlled_buffer_1_out = decoder_2_out8 ? register_9_q : 8'bz;  // Controlled_Buffer controlled_buffer_18
  Register register_10 (.D(data), .Q(register_10_q), .clk(decoder_3_out9));  // open: en, clr
  assign controlled_buffer_2_out = decoder_1_out9 ? register_10_q : 8'bz;  // Controlled_Buffer controlled_buffer_19
  assign controlled_buffer_1_out = decoder_2_out9 ? register_10_q : 8'bz;  // Controlled_Buffer controlled_buffer_20
  Register register_11 (.D(data), .Q(register_11_q), .clk(decoder_3_out11));  // open: en, clr
  Register register_12 (.D(data), .Q(register_12_q), .clk(decoder_3_out10));  // open: en, clr
  assign controlled_buffer_1_out = decoder_2_out11 ? register_11_q : 8'bz;  // Controlled_Buffer controlled_buffer_21
  assign controlled_buffer_2_out = decoder_1_out10 ? register_12_q : 8'bz;  // Controlled_Buffer controlled_buffer_22
  assign controlled_buffer_1_out = decoder_2_out10 ? register_12_q : 8'bz;  // Controlled_Buffer controlled_buffer_23
  Register register_13 (.D(data), .Q(register_13_q), .clk(decoder_3_out12));  // open: en, clr
  assign controlled_buffer_2_out = decoder_1_out11 ? register_11_q : 8'bz;  // Controlled_Buffer controlled_buffer_24
  assign controlled_buffer_1_out = decoder_2_out12 ? register_13_q : 8'bz;  // Controlled_Buffer controlled_buffer_25
  assign controlled_buffer_2_out = decoder_1_out12 ? register_13_q : 8'bz;  // Controlled_Buffer controlled_buffer_26
  Register register_14 (.D(data), .Q(register_14_q), .clk(decoder_3_out13));  // open: en, clr
  assign controlled_buffer_1_out = decoder_2_out13 ? register_14_q : 8'bz;  // Controlled_Buffer controlled_buffer_27
  assign controlled_buffer_2_out = decoder_1_out13 ? register_14_q : 8'bz;  // Controlled_Buffer controlled_buffer_28
  Register register_15 (.D(data), .Q(register_15_q), .clk(decoder_3_out14));  // open: en, clr
  assign controlled_buffer_1_out = decoder_2_out14 ? register_15_q : 8'bz;  // Controlled_Buffer controlled_buffer_29
  assign controlled_buffer_2_out = decoder_1_out14 ? register_15_q : 8'bz;  // Controlled_Buffer controlled_buffer_30
  Register register_16 (.D(data), .Q(register_16_q), .clk(decoder_3_out15));  // open: en, clr
  assign controlled_buffer_2_out = decoder_1_out15 ? register_16_q : 8'bz;  // Controlled_Buffer controlled_buffer_31
  assign controlled_buffer_1_out = decoder_2_out15 ? register_16_q : 8'bz;  // Controlled_Buffer controlled_buffer_32
  Register #(.trigger("high")) register_17 (.D(controlled_buffer_2_out), .Q(A), .clk(clock));  // open: en, clr
  Register #(.trigger("high")) register_18 (.D(controlled_buffer_1_out), .Q(B), .clk(clock));  // open: en, clr
endmodule

// command unit
module cu (
  input  clock,
  input  [15:0] instruction,
  input  cout,
  input  interrupt,
  input  zero,
  input  A_B,
  output [8:0] jump_address,
  output [3:0] save_reg,
  output [7:0] immediate_data,
  output [3:0] read_b,
  output [3:0] read_a,
  output [3:0] alu_opcode,
  output save,
  output save_to_memory,
  output load_from_memory,
  output enable_cin,
  output io_call,
  output external_input,
  output load_immediate,
  output jump_active
);

  wire A_B_q, and_1_out, and_2_out, and_3_out, and_4_out, and_5_out, and_6_out, and_7_out, and_8_out,
       decoder_1_out0, decoder_1_out1, decoder_1_out2, decoder_1_out3, decoder_1_out4, decoder_1_out5,
       decoder_1_out6, decoder_1_out7, decoder_1_out8, decoder_1_out12, decoder_1_out14, decoder_1_out15,
       decoder_2_out0, decoder_2_out1, decoder_2_out2, decoder_2_out3, decoder_2_out7, interrupt_q, or_1_out,
       or_2_out, or_3_out, or_4_out, or_5_out, or_9_out, overflow_q, zero_q;
  wire [15:15] IR_q;

  Register #(.width(16), .trigger("high")) IR (
    .D(instruction), .Q({IR_q[15], alu_opcode[2:0], immediate_data, jump_address[3:0]}), .clk(clock));  // open: en, clr
  and and_1 (and_1_out, or_4_out, ~clock);  // AND_Gate
  and and_2 (and_2_out, io_call, ~clock);  // AND_Gate
  and and_3 (and_3_out, or_3_out, ~clock);  // AND_Gate
  and and_4 (and_4_out, decoder_1_out8, ~clock);  // AND_Gate
  or or_1 (or_1_out, or_3_out, io_call, decoder_1_out0, load_from_memory, load_immediate);
  and and_5 (and_5_out, decoder_2_out2, overflow_q);
  D_Flip_Flop overflow (.clk(and_1_out), .D(cout), .Q(overflow_q));  // open: Qn, preset, en, reset
  and and_6 (and_6_out, decoder_2_out7, interrupt_q);
  D_Flip_Flop u_interrupt (.clk(and_2_out), .D(interrupt), .Q(interrupt_q));  // open: Qn, preset, en, reset
  and and_7 (and_7_out, decoder_2_out1, zero_q);
  D_Flip_Flop u_zero (.clk(and_3_out), .D(zero), .Q(zero_q));  // open: Qn, preset, en, reset
  and and_8 (and_8_out, decoder_2_out3, A_B_q);
  D_Flip_Flop u_A_B (.clk(and_4_out), .D(A_B), .Q(A_B_q));  // open: Qn, preset, en, reset
  and and_9 (save, ~clock, or_1_out);  // AND_Gate
  or or_2 (or_2_out, decoder_1_out1, decoder_1_out2, decoder_1_out3, decoder_1_out4, decoder_1_out5, decoder_1_out6, decoder_1_out7);
  or or_3 (or_3_out, or_2_out, decoder_1_out15, decoder_1_out14);
  or or_4 (or_4_out, or_5_out, decoder_1_out15);
  or or_5 (or_5_out, decoder_1_out1, decoder_1_out2, decoder_1_out7);
  Decoder #(.select(4), .disabled(0), .enable("false")) decoder_1 (
    .out0(decoder_1_out0), .out1(decoder_1_out1), .out2(decoder_1_out2), .out3(decoder_1_out3),
    .out4(decoder_1_out4), .out5(decoder_1_out5), .out6(decoder_1_out6), .out7(decoder_1_out7),
    .out8(decoder_1_out8), .out9(io_call), .out10(save_to_memory), .out11(load_from_memory),
    .out12(decoder_1_out12), .out13(load_immediate), .out14(decoder_1_out14), .out15(decoder_1_out15),
    .sel({IR_q[15], alu_opcode[2:0]}));
  or or_6 (alu_opcode[3], decoder_1_out14, decoder_1_out15);
  or or_7 (enable_cin, decoder_1_out2, decoder_1_out7);
  or or_8 (external_input, load_from_memory, io_call);
  Decoder #(.select(3), .disabled(0), .enable("false")) decoder_2 (
    .out0(decoder_2_out0), .out1(decoder_2_out1), .out2(decoder_2_out2), .out3(decoder_2_out3),
    .out7(decoder_2_out7), .sel(immediate_data[7:5]));  // open: out4, out5, out6
  and and_10 (jump_active, decoder_1_out12, or_9_out);
  or or_9 (or_9_out, decoder_2_out0, and_5_out, and_6_out, and_7_out, and_8_out);

  assign jump_address[8:4] = immediate_data[4:0];
  assign read_a = immediate_data[7:4];
  assign read_b = immediate_data[3:0];
  assign save_reg = jump_address[3:0];
endmodule

// BC1
module cpu (
  input  clock,
  input  interrupt,
  input  [15:0] instruction,
  input  [7:0] data_in,
  input  [7:0] memory_data_in,
  output [8:0] instruction_address,
  output write_to_memory,
  output [3:0] io_port,
  output [7:0] data_out,
  output [7:0] memory_address
);

  wire alu_1_a_b, alu_1_cout, alu_1_zero, cu_1_enable_cin, cu_1_external_input, cu_1_io_call,
       cu_1_jump_active, cu_1_load_from_memory, cu_1_load_immediate, cu_1_save, not_1_out;
  wire [3:0] cu_1_alu_opcode, cu_1_read_a, cu_1_read_b, cu_1_save_reg;
  wire [7:0] alu_1_c, cu_1_immediate_data, multiplexer_1_out, multiplexer_2_out, multiplexer_3_out;
  wire [8:0] cu_1_jump_address;

  Multiplexer #(.width(8), .disabled(0), .enable("false")) multiplexer_1 (
    .in0(data_in), .in1(memory_data_in), .out(multiplexer_1_out), .sel(cu_1_load_from_memory));
  not not_1 (not_1_out, cu_1_jump_active);
  cu cu_1 (
    .clock(clock), .instruction(instruction), .cout(alu_1_cout), .jump_address(cu_1_jump_address),
    .save_reg(cu_1_save_reg), .save_to_memory(write_to_memory), .load_from_memory(cu_1_load_from_memory),
    .read_b(cu_1_read_b), .external_input(cu_1_external_input), .read_a(cu_1_read_a),
    .alu_opcode(cu_1_alu_opcode), .enable_cin(cu_1_enable_cin), .jump_active(cu_1_jump_active),
    .save(cu_1_save), .io_call(cu_1_io_call), .interrupt(interrupt), .zero(alu_1_zero), .A_B(alu_1_a_b),
    .immediate_data(cu_1_immediate_data), .load_immediate(cu_1_load_immediate));
  Multiplexer #(.width(8), .disabled(0), .enable("false")) multiplexer_2 (
    .in0(alu_1_c), .in1(cu_1_immediate_data), .out(multiplexer_2_out), .sel(cu_1_load_immediate));
  Counter #(.width(9), .max('h1ff)) counter_1 (
    .load(cu_1_jump_active), .D(cu_1_jump_address), .count(not_1_out), .Q(instruction_address), .clk(clock));  // open: carry, clr
  Multiplexer #(.width(8), .disabled(0), .enable("false")) multiplexer_3 (
    .in0(multiplexer_2_out), .in1(multiplexer_1_out), .out(multiplexer_3_out), .sel(cu_1_external_input));
  alu alu_1 (
    .alu_opcode(cu_1_alu_opcode), .cin(cu_1_enable_cin), .A(memory_address), .B(data_out), .cout(alu_1_cout),
    .C(alu_1_c), .zero(alu_1_zero), .A_B(alu_1_a_b));
  register_file register_file_1 (
    .read_A(cu_1_read_a), .read_B(cu_1_read_b), .save_reg(cu_1_save_reg), .A(memory_address), .B(data_out),
    .save(cu_1_save), .data(multiplexer_3_out), .clock(clock));
  assign io_port = cu_1_io_call ? cu_1_read_a : 4'bz;  // Controlled_Buffer controlled_buffer_1
  Pull_Resistor pull_resistor_1 (.node(io_port));
endmodule

// io bus splitter
module io_splitter (
  input  [7:0] data_out,
  input  [7:0] port_1_data_in,
  input  port_1_interrupt_line,
  input  clock,
  input  [3:0] port,
  input  [7:0] port_2_data_in,
  input  port_2_interrupt_line,
  input  [7:0] port_3_data_in,
  input  port_3_interrupt_line,
  output [7:0] port_1_data_out,
  output port_1_data_ready,
  output [7:0] port_2_data_out,
  output port_2_data_ready,
  output [7:0] port_3_data_out,
  output interrupt,
  output port_3_data_ready,
  output [7:0] data_to_cpu
);

  wire and_1_out, and_2_out, and_3_out, decoder_2_out1, decoder_2_out2, decoder_2_out3, not_1_out;

  not not_1 (not_1_out, clock);
  Decoder #(.select(2), .disabled(0)) decoder_1 (
    .out1(port_1_data_ready), .out2(port_2_data_ready), .out3(port_3_data_ready), .sel(port[1:0]),
    .en(not_1_out));  // open: out0
  Decoder #(.select(2), .disabled(0), .enable("false")) decoder_2 (
    .out1(decoder_2_out1), .out2(decoder_2_out2), .out3(decoder_2_out3), .sel(port[3:2]));  // open: out0
  and and_1 (and_1_out, decoder_2_out2, port_2_interrupt_line);
  and and_2 (and_2_out, decoder_2_out3, port_3_interrupt_line);
  or or_1 (interrupt, and_2_out, and_1_out, and_3_out);
  and and_3 (and_3_out, decoder_2_out1, port_1_interrupt_line);
  Multiplexer #(.select(2), .width(8), .disabled(0), .enable("false")) multiplexer_1 (
    .in0({8{1'b0}}), .in1(port_1_data_in), .in2(port_2_data_in), .in3(port_3_data_in), .out(data_to_cpu),
    .sel(port[3:2]));

  assign port_1_data_out = data_out;
  assign port_2_data_out = data_out;
  assign port_3_data_out = data_out;
endmodule

module frame_buffer (
  input  [7:0] data_in,
  input  update,
  output [15:0] out_3,
  output [15:0] out_4,
  output [15:0] out_5,
  output [15:0] out_6,
  output [15:0] out_7,
  output [15:0] out_8,
  output [15:0] out_9,
  output [15:0] out_10,
  output [15:0] out_11,
  output [15:0] out_12,
  output [15:0] out_13,
  output [15:0] out_14,
  output [15:0] out_15,
  output [15:0] out_16,
  output [15:0] out_17,
  output [15:0] out_18
);

  wire and_1_out, and_2_out, and_3_out, and_4_out, and_5_out, and_6_out, and_7_out, and_8_out, and_9_out,
       and_10_out, and_11_out, and_12_out, and_13_out, and_14_out, and_15_out, and_16_out, and_17_out,
       and_18_out, and_19_out, and_20_out, and_21_out, and_22_out, and_23_out, and_24_out, and_25_out,
       and_26_out, and_27_out, and_28_out, and_29_out, and_30_out, and_31_out, and_32_out, and_33_out,
       and_34_out, and_35_out, and_36_out, and_37_out, and_38_out, and_39_out, and_40_out, and_41_out,
       and_42_out, and_43_out, and_44_out, and_45_out, and_46_out, and_47_out, and_48_out, and_49_out,
       and_50_out, and_51_out, and_52_out, and_53_out, and_54_out, and_55_out, and_56_out, and_57_out,
       and_58_out, and_59_out, and_60_out, and_61_out, and_62_out, and_63_out, and_64_out, and_65_out,
       and_66_out, and_67_out, and_68_out, and_69_out, and_70_out, and_71_out, and_72_out, and_73_out,
       and_74_out, and_75_out, and_76_out, and_77_out, and_78_out, and_79_out, and_80_out, and_81_out,
       and_82_out, and_83_out, and_84_out, and_85_out, and_86_out, and_87_out, and_88_out, and_89_out,
       and_90_out, and_91_out, and_92_out, and_93_out, and_94_out, and_95_out, and_96_out, and_97_out,
       and_98_out, and_99_out, and_100_out, and_101_out, and_102_out, and_103_out, and_104_out, and_105_out,
       and_106_out, and_107_out, and_108_out, and_109_out, and_110_out, and_111_out, and_112_out,
       and_113_out, and_114_out, and_115_out, and_116_out, and_117_out, and_118_out, and_119_out,
       and_120_out, and_121_out, and_122_out, and_123_out, and_124_out, and_125_out, and_126_out,
       and_127_out, and_128_out, and_129_out, and_130_out, and_131_out, and_132_out, and_133_out,
       and_134_out, and_135_out, and_136_out, and_137_out, and_138_out, and_139_out, and_140_out,
       and_141_out, and_142_out, and_143_out, and_144_out, and_145_out, and_146_out, and_147_out,
       and_148_out, and_149_out, and_150_out, and_151_out, and_152_out, and_153_out, and_154_out,
       and_155_out, and_156_out, and_157_out, and_158_out, and_159_out, and_160_out, and_161_out,
       and_162_out, and_163_out, and_164_out, and_165_out, and_166_out, and_167_out, and_168_out,
       and_169_out, and_170_out, and_171_out, and_172_out, and_173_out, and_174_out, and_175_out,
       and_176_out, and_177_out, and_178_out, and_179_out, and_180_out, and_181_out, and_182_out,
       and_183_out, and_184_out, and_185_out, and_186_out, and_187_out, and_188_out, and_189_out,
       and_190_out, and_191_out, and_192_out, and_193_out, and_194_out, and_195_out, and_196_out,
       and_197_out, and_198_out, and_199_out, and_200_out, and_201_out, and_202_out, and_203_out,
       and_204_out, and_205_out, and_206_out, and_207_out, and_208_out, and_209_out, and_210_out,
       and_211_out, and_212_out, and_213_out, and_214_out, and_215_out, and_216_out, and_217_out,
       and_218_out, and_219_out, and_220_out, and_221_out, and_222_out, and_223_out, and_224_out,
       and_225_out, and_226_out, and_227_out, and_228_out, and_229_out, and_230_out, and_231_out,
       and_232_out, and_233_out, and_234_out, and_235_out, and_236_out, and_237_out, and_238_out,
       and_239_out, and_240_out, and_241_out, and_242_out, and_243_out, and_244_out, and_245_out,
       and_246_out, and_247_out, and_248_out, and_249_out, and_250_out, and_251_out, and_252_out,
       and_253_out, and_254_out, and_255_out, and_256_out, decoder_1_out0, decoder_1_out1, decoder_1_out2,
       decoder_1_out3, decoder_1_out4, decoder_1_out5, decoder_1_out6, decoder_1_out7, decoder_1_out8,
       decoder_1_out9, decoder_1_out10, decoder_1_out11, decoder_1_out12, decoder_1_out13, decoder_1_out14,
       decoder_1_out15, decoder_2_out0, decoder_2_out1, decoder_2_out2, decoder_2_out3, decoder_2_out4,
       decoder_2_out5, decoder_2_out6, decoder_2_out7, decoder_2_out8, decoder_2_out9, decoder_2_out10,
       decoder_2_out11, decoder_2_out12, decoder_2_out13, decoder_2_out14, decoder_2_out15;

  Decoder #(.select(4), .disabled(0)) decoder_1 (
    .out0(decoder_1_out0), .out1(decoder_1_out1), .out2(decoder_1_out2), .out3(decoder_1_out3),
    .out4(decoder_1_out4), .out5(decoder_1_out5), .out6(decoder_1_out6), .out7(decoder_1_out7),
    .out8(decoder_1_out8), .out9(decoder_1_out9), .out10(decoder_1_out10), .out11(decoder_1_out11),
    .out12(decoder_1_out12), .out13(decoder_1_out13), .out14(decoder_1_out14), .out15(decoder_1_out15),
    .sel(data_in[3:0]), .en(update));
  Decoder #(.select(4), .disabled(0)) decoder_2 (
    .out0(decoder_2_out0), .out1(decoder_2_out1), .out2(decoder_2_out2), .out3(decoder_2_out3),
    .out4(decoder_2_out4), .out5(decoder_2_out5), .out6(decoder_2_out6), .out7(decoder_2_out7),
    .out8(decoder_2_out8), .out9(decoder_2_out9), .out10(decoder_2_out10), .out11(decoder_2_out11),
    .out12(decoder_2_out12), .out13(decoder_2_out13), .out14(decoder_2_out14), .out15(decoder_2_out15),
    .sel(data_in[7:4]), .en(update));
  T_Flip_Flop t_ff_1 (.clk(and_1_out), .T(and_1_out), .Q(out_3[0]));  // open: Qn, preset, reset, en
  and and_1 (and_1_out, decoder_1_out0, decoder_2_out0);
  T_Flip_Flop t_ff_2 (.clk(and_2_out), .T(and_2_out), .Q(out_4[0]));  // open: Qn, preset, reset, en
  and and_2 (and_2_out, decoder_1_out0, decoder_2_out1);
  T_Flip_Flop t_ff_3 (.clk(and_3_out), .T(and_3_out), .Q(out_5[0]));  // open: Qn, preset, reset, en
  and and_3 (and_3_out, decoder_1_out0, decoder_2_out2);
  and and_4 (and_4_out, decoder_1_out0, decoder_2_out3);
  T_Flip_Flop t_ff_4 (.clk(and_4_out), .T(and_4_out), .Q(out_6[0]));  // open: Qn, preset, reset, en
  and and_5 (and_5_out, decoder_1_out0, decoder_2_out4);
  T_Flip_Flop t_ff_5 (.clk(and_5_out), .T(and_5_out), .Q(out_7[0]));  // open: Qn, preset, reset, en
  and and_6 (and_6_out, decoder_1_out0, decoder_2_out5);
  T_Flip_Flop t_ff_6 (.clk(and_6_out), .T(and_6_out), .Q(out_8[0]));  // open: Qn, preset, reset, en
  T_Flip_Flop t_ff_7 (.clk(and_7_out), .T(and_7_out), .Q(out_9[0]));  // open: Qn, preset, reset, en
  and and_7 (and_7_out, decoder_1_out0, decoder_2_out6);
  and and_8 (and_8_out, decoder_1_out0, decoder_2_out7);
  T_Flip_Flop t_ff_8 (.clk(and_8_out), .T(and_8_out), .Q(out_10[0]));  // open: Qn, preset, reset, en
  and and_9 (and_9_out, decoder_1_out0, decoder_2_out8);
  T_Flip_Flop t_ff_9 (.clk(and_9_out), .T(and_9_out), .Q(out_11[0]));  // open: Qn, preset, reset, en
  T_Flip_Flop t_ff_10 (.clk(and_10_out), .T(and_10_out), .Q(out_12[0]));  // open: Qn, preset, reset, en
  and and_10 (and_10_out, decoder_1_out0, decoder_2_out9);
  T_Flip_Flop t_ff_11 (.clk(and_11_out), .T(and_11_out), .Q(out_13[0]));  // open: Qn, preset, reset, en
  and and_11 (and_11_out, decoder_1_out0, decoder_2_out10);
  and and_12 (and_12_out, decoder_1_out0, decoder_2_out11);
  T_Flip_Flop t_ff_12 (.clk(and_12_out), .T(and_12_out), .Q(out_14[0]));  // open: Qn, preset, reset, en
  T_Flip_Flop t_ff_13 (.clk(and_13_out), .T(and_13_out), .Q(out_15[0]));  // open: Qn, preset, reset, en
  and and_13 (and_13_out, decoder_1_out0, decoder_2_out12);
  and and_14 (and_14_out, decoder_1_out0, decoder_2_out13);
  T_Flip_Flop t_ff_14 (.clk(and_14_out), .T(and_14_out), .Q(out_16[0]));  // open: Qn, preset, reset, en
  and and_15 (and_15_out, decoder_1_out0, decoder_2_out14);
  T_Flip_Flop t_ff_15 (.clk(and_15_out), .T(and_15_out), .Q(out_17[0]));  // open: Qn, preset, reset, en
  and and_16 (and_16_out, decoder_1_out0, decoder_2_out15);
  T_Flip_Flop t_ff_16 (.clk(and_16_out), .T(and_16_out), .Q(out_18[0]));  // open: Qn, preset, reset, en
  and and_17 (and_17_out, decoder_1_out1, decoder_2_out0);
  T_Flip_Flop t_ff_17 (.clk(and_17_out), .T(and_17_out), .Q(out_3[1]));  // open: Qn, preset, reset, en
  and and_18 (and_18_out, decoder_1_out1, decoder_2_out1);
  T_Flip_Flop t_ff_18 (.clk(and_18_out), .T(and_18_out), .Q(out_4[1]));  // open: Qn, preset, reset, en
  and and_19 (and_19_out, decoder_1_out1, decoder_2_out2);
  T_Flip_Flop t_ff_19 (.clk(and_19_out), .T(and_19_out), .Q(out_5[1]));  // open: Qn, preset, reset, en
  T_Flip_Flop t_ff_20 (.clk(and_20_out), .T(and_20_out), .Q(out_6[1]));  // open: Qn, preset, reset, en
  and and_20 (and_20_out, decoder_1_out1, decoder_2_out3);
  T_Flip_Flop t_ff_21 (.clk(and_21_out), .T(and_21_out), .Q(out_7[1]));  // open: Qn, preset, reset, en
  and and_21 (and_21_out, decoder_1_out1, decoder_2_out4);
  and and_22 (and_22_out, decoder_1_out1, decoder_2_out5);
  T_Flip_Flop t_ff_22 (.clk(and_22_out), .T(and_22_out), .Q(out_8[1]));  // open: Qn, preset, reset, en
  and and_23 (and_23_out, decoder_1_out1, decoder_2_out6);
  T_Flip_Flop t_ff_23 (.clk(and_23_out), .T(and_23_out), .Q(out_9[1]));  // open: Qn, preset, reset, en
  and and_24 (and_24_out, decoder_1_out1, decoder_2_out7);
  T_Flip_Flop t_ff_24 (.clk(and_24_out), .T(and_24_out), .Q(out_10[1]));  // open: Qn, preset, reset, en
  and and_25 (and_25_out, decoder_1_out1, decoder_2_out8);
  T_Flip_Flop t_ff_25 (.clk(and_25_out), .T(and_25_out), .Q(out_11[1]));  // open: Qn, preset, reset, en
  and and_26 (and_26_out, decoder_1_out1, decoder_2_out9);
  T_Flip_Flop t_ff_26 (.clk(and_26_out), .T(and_26_out), .Q(out_12[1]));  // open: Qn, preset, reset, en
  T_Flip_Flop t_ff_27 (.clk(and_27_out), .T(and_27_out), .Q(out_13[1]));  // open: Qn, preset, reset, en
  and and_27 (and_27_out, decoder_1_out1, decoder_2_out10);
  and and_28 (and_28_out, decoder_1_out1, decoder_2_out11);
  T_Flip_Flop t_ff_28 (.clk(and_28_out), .T(and_28_out), .Q(out_14[1]));  // open: Qn, preset, reset, en
  T_Flip_Flop t_ff_29 (.clk(and_29_out), .T(and_29_out), .Q(out_15[1]));  // open: Qn, preset, reset, en
  and and_29 (and_29_out, decoder_1_out1, decoder_2_out12);
  T_Flip_Flop t_ff_30 (.clk(and_30_out), .T(and_30_out), .Q(out_16[1]));  // open: Qn, preset, reset, en
  and and_30 (and_30_out, decoder_1_out1, decoder_2_out13);
  and and_31 (and_31_out, decoder_1_out1, decoder_2_out14);
  T_Flip_Flop t_ff_31 (.clk(and_31_out), .T(and_31_out), .Q(out_17[1]));  // open: Qn, preset, reset, en
  T_Flip_Flop t_ff_32 (.clk(and_32_out), .T(and_32_out), .Q(out_18[1]));  // open: Qn, preset, reset, en
  and and_32 (and_32_out, decoder_1_out1, decoder_2_out15);
  and and_33 (and_33_out, decoder_1_out2, decoder_2_out0);
  T_Flip_Flop t_ff_33 (.clk(and_33_out), .T(and_33_out), .Q(out_3[2]));  // open: Qn, preset, reset, en
  T_Flip_Flop t_ff_34 (.clk(and_34_out), .T(and_34_out), .Q(out_4[2]));  // open: Qn, preset, reset, en
  and and_34 (and_34_out, decoder_1_out2, decoder_2_out1);
  and and_35 (and_35_out, decoder_1_out2, decoder_2_out2);
  T_Flip_Flop t_ff_35 (.clk(and_35_out), .T(and_35_out), .Q(out_5[2]));  // open: Qn, preset, reset, en
  and and_36 (and_36_out, decoder_1_out2, decoder_2_out3);
  T_Flip_Flop t_ff_36 (.clk(and_36_out), .T(and_36_out), .Q(out_6[2]));  // open: Qn, preset, reset, en
  and and_37 (and_37_out, decoder_1_out2, decoder_2_out4);
  T_Flip_Flop t_ff_37 (.clk(and_37_out), .T(and_37_out), .Q(out_7[2]));  // open: Qn, preset, reset, en
  T_Flip_Flop t_ff_38 (.clk(and_38_out), .T(and_38_out), .Q(out_8[2]));  // open: Qn, preset, reset, en
  and and_38 (and_38_out, decoder_1_out2, decoder_2_out5);
  T_Flip_Flop t_ff_39 (.clk(and_39_out), .T(and_39_out), .Q(out_9[2]));  // open: Qn, preset, reset, en
  and and_39 (and_39_out, decoder_1_out2, decoder_2_out6);
  and and_40 (and_40_out, decoder_1_out2, decoder_2_out7);
  T_Flip_Flop t_ff_40 (.clk(and_40_out), .T(and_40_out), .Q(out_10[2]));  // open: Qn, preset, reset, en
  and and_41 (and_41_out, decoder_1_out2, decoder_2_out8);
  T_Flip_Flop t_ff_41 (.clk(and_41_out), .T(and_41_out), .Q(out_11[2]));  // open: Qn, preset, reset, en
  T_Flip_Flop t_ff_42 (.clk(and_42_out), .T(and_42_out), .Q(out_12[2]));  // open: Qn, preset, reset, en
  and and_42 (and_42_out, decoder_1_out2, decoder_2_out9);
  and and_43 (and_43_out, decoder_1_out2, decoder_2_out10);
  T_Flip_Flop t_ff_43 (.clk(and_43_out), .T(and_43_out), .Q(out_13[2]));  // open: Qn, preset, reset, en
  and and_44 (and_44_out, decoder_1_out2, decoder_2_out11);
  T_Flip_Flop t_ff_44 (.clk(and_44_out), .T(and_44_out), .Q(out_14[2]));  // open: Qn, preset, reset, en
  and and_45 (and_45_out, decoder_1_out2, decoder_2_out12);
  T_Flip_Flop t_ff_45 (.clk(and_45_out), .T(and_45_out), .Q(out_15[2]));  // open: Qn, preset, reset, en
  and and_46 (and_46_out, decoder_1_out2, decoder_2_out13);
  T_Flip_Flop t_ff_46 (.clk(and_46_out), .T(and_46_out), .Q(out_16[2]));  // open: Qn, preset, reset, en
  T_Flip_Flop t_ff_47 (.clk(and_47_out), .T(and_47_out), .Q(out_17[2]));  // open: Qn, preset, reset, en
  and and_47 (and_47_out, decoder_1_out2, decoder_2_out14);
  and and_48 (and_48_out, decoder_1_out2, decoder_2_out15);
  T_Flip_Flop t_ff_48 (.clk(and_48_out), .T(and_48_out), .Q(out_18[2]));  // open: Qn, preset, reset, en
  and and_49 (and_49_out, decoder_1_out3, decoder_2_out0);
  T_Flip_Flop t_ff_49 (.clk(and_49_out), .T(and_49_out), .Q(out_3[3]));  // open: Qn, preset, reset, en
  T_Flip_Flop t_ff_50 (.clk(and_50_out), .T(and_50_out), .Q(out_4[3]));  // open: Qn, preset, reset, en
  and and_50 (and_50_out, decoder_1_out3, decoder_2_out1);
  and and_51 (and_51_out, decoder_1_out3, decoder_2_out2);
  T_Flip_Flop t_ff_51 (.clk(and_51_out), .T(and_51_out), .Q(out_5[3]));  // open: Qn, preset, reset, en
  T_Flip_Flop t_ff_52 (.clk(and_52_out), .T(and_52_out), .Q(out_6[3]));  // open: Qn, preset, reset, en
  and and_52 (and_52_out, decoder_1_out3, decoder_2_out3);
  T_Flip_Flop t_ff_53 (.clk(and_53_out), .T(and_53_out), .Q(out_7[3]));  // open: Qn, preset, reset, en
  and and_53 (and_53_out, decoder_1_out3, decoder_2_out4);
  T_Flip_Flop t_ff_54 (.clk(and_54_out), .T(and_54_out), .Q(out_8[3]));  // open: Qn, preset, reset, en
  and and_54 (and_54_out, decoder_1_out3, decoder_2_out5);
  T_Flip_Flop t_ff_55 (.clk(and_55_out), .T(and_55_out), .Q(out_9[3]));  // open: Qn, preset, reset, en
  and and_55 (and_55_out, decoder_1_out3, decoder_2_out6);
  and and_56 (and_56_out, decoder_1_out3, decoder_2_out7);
  T_Flip_Flop t_ff_56 (.clk(and_56_out), .T(and_56_out), .Q(out_10[3]));  // open: Qn, preset, reset, en
  and and_57 (and_57_out, decoder_1_out3, decoder_2_out8);
  T_Flip_Flop t_ff_57 (.clk(and_57_out), .T(and_57_out), .Q(out_11[3]));  // open: Qn, preset, reset, en
  and and_58 (and_58_out, decoder_1_out3, decoder_2_out9);
  T_Flip_Flop t_ff_58 (.clk(and_58_out), .T(and_58_out), .Q(out_12[3]));  // open: Qn, preset, reset, en
  and and_59 (and_59_out, decoder_1_out3, decoder_2_out10);
  T_Flip_Flop t_ff_59 (.clk(and_59_out), .T(and_59_out), .Q(out_13[3]));  // open: Qn, preset, reset, en
  and and_60 (and_60_out, decoder_1_out3, decoder_2_out11);
  T_Flip_Flop t_ff_60 (.clk(and_60_out), .T(and_60_out), .Q(out_14[3]));  // open: Qn, preset, reset, en
  and and_61 (and_61_out, decoder_1_out3, decoder_2_out12);
  T_Flip_Flop t_ff_61 (.clk(and_61_out), .T(and_61_out), .Q(out_15[3]));  // open: Qn, preset, reset, en
  and and_62 (and_62_out, decoder_1_out3, decoder_2_out13);
  T_Flip_Flop t_ff_62 (.clk(and_62_out), .T(and_62_out), .Q(out_16[3]));  // open: Qn, preset, reset, en
  T_Flip_Flop t_ff_63 (.clk(and_63_out), .T(and_63_out), .Q(out_17[3]));  // open: Qn, preset, reset, en
  and and_63 (and_63_out, decoder_1_out3, decoder_2_out14);
  T_Flip_Flop t_ff_64 (.clk(and_64_out), .T(and_64_out), .Q(out_18[3]));  // open: Qn, preset, reset, en
  and and_64 (and_64_out, decoder_1_out3, decoder_2_out15);
  T_Flip_Flop t_ff_65 (.clk(and_65_out), .T(and_65_out), .Q(out_3[4]));  // open: Qn, preset, reset, en
  and and_65 (and_65_out, decoder_1_out4, decoder_2_out0);
  and and_66 (and_66_out, decoder_1_out5, decoder_2_out0);
  and and_67 (and_67_out, decoder_1_out5, decoder_2_out1);
  T_Flip_Flop t_ff_66 (.clk(and_68_out), .T(and_68_out), .Q(out_4[4]));  // open: Qn, preset, reset, en
  and and_68 (and_68_out, decoder_1_out4, decoder_2_out1);
  and and_69 (and_69_out, decoder_1_out5, decoder_2_out2);
  and and_70 (and_70_out, decoder_1_out4, decoder_2_out2);
  T_Flip_Flop t_ff_67 (.clk(and_70_out), .T(and_70_out), .Q(out_5[4]));  // open: Qn, preset, reset, en
  T_Flip_Flop t_ff_68 (.clk(and_72_out), .T(and_72_out), .Q(out_6[4]));  // open: Qn, preset, reset, en
  and and_71 (and_71_out, decoder_1_out5, decoder_2_out3);
  and and_72 (and_72_out, decoder_1_out4, decoder_2_out3);
  and and_73 (and_73_out, decoder_1_out5, decoder_2_out4);
  T_Flip_Flop t_ff_69 (.clk(and_74_out), .T(and_74_out), .Q(out_7[4]));  // open: Qn, preset, reset, en
  and and_74 (and_74_out, decoder_1_out4, decoder_2_out4);
  and and_75 (and_75_out, decoder_1_out4, decoder_2_out5);
  T_Flip_Flop t_ff_70 (.clk(and_75_out), .T(and_75_out), .Q(out_8[4]));  // open: Qn, preset, reset, en
  and and_76 (and_76_out, decoder_1_out5, decoder_2_out5);
  and and_77 (and_77_out, decoder_1_out4, decoder_2_out6);
  and and_78 (and_78_out, decoder_1_out5, decoder_2_out6);
  T_Flip_Flop t_ff_71 (.clk(and_77_out), .T(and_77_out), .Q(out_9[4]));  // open: Qn, preset, reset, en
  and and_79 (and_79_out, decoder_1_out4, decoder_2_out7);
  and and_80 (and_80_out, decoder_1_out5, decoder_2_out7);
  T_Flip_Flop t_ff_72 (.clk(and_79_out), .T(and_79_out), .Q(out_10[4]));  // open: Qn, preset, reset, en
  T_Flip_Flop t_ff_73 (.clk(and_81_out), .T(and_81_out), .Q(out_11[4]));  // open: Qn, preset, reset, en
  and and_81 (and_81_out, decoder_1_out4, decoder_2_out8);
  and and_82 (and_82_out, decoder_1_out5, decoder_2_out8);
  T_Flip_Flop t_ff_74 (.clk(and_84_out), .T(and_84_out), .Q(out_12[4]));  // open: Qn, preset, reset, en
  and and_83 (and_83_out, decoder_1_out5, decoder_2_out9);
  and and_84 (and_84_out, decoder_1_out4, decoder_2_out9);
  and and_85 (and_85_out, decoder_1_out5, decoder_2_out10);
  T_Flip_Flop t_ff_75 (.clk(and_86_out), .T(and_86_out), .Q(out_13[4]));  // open: Qn, preset, reset, en
  and and_86 (and_86_out, decoder_1_out4, decoder_2_out10);
  and and_87 (and_87_out, decoder_1_out4, decoder_2_out11);
  and and_88 (and_88_out, decoder_1_out5, decoder_2_out11);
  T_Flip_Flop t_ff_76 (.clk(and_87_out), .T(and_87_out), .Q(out_14[4]));  // open: Qn, preset, reset, en
  T_Flip_Flop t_ff_77 (.clk(and_89_out), .T(and_89_out), .Q(out_15[4]));  // open: Qn, preset, reset, en
  and and_89 (and_89_out, decoder_1_out4, decoder_2_out12);
  and and_90 (and_90_out, decoder_1_out5, decoder_2_out12);
  and and_91 (and_91_out, decoder_1_out5, decoder_2_out13);
  and and_92 (and_92_out, decoder_1_out4, decoder_2_out13);
  T_Flip_Flop t_ff_78 (.clk(and_92_out), .T(and_92_out), .Q(out_16[4]));  // open: Qn, preset, reset, en
  and and_93 (and_93_out, decoder_1_out4, decoder_2_out14);
  T_Flip_Flop t_ff_79 (.clk(and_93_out), .T(and_93_out), .Q(out_17[4]));  // open: Qn, preset, reset, en
  and and_94 (and_94_out, decoder_1_out5, decoder_2_out14);
  and and_95 (and_95_out, decoder_1_out4, decoder_2_out15);
  and and_96 (and_96_out, decoder_1_out5, decoder_2_out15);
  T_Flip_Flop t_ff_80 (.clk(and_95_out), .T(and_95_out), .Q(out_18[4]));  // open: Qn, preset, reset, en
  T_Flip_Flop t_ff_81 (.clk(and_66_out), .T(and_66_out), .Q(out_3[5]));  // open: Qn, preset, reset, en
  and and_97 (and_97_out, decoder_1_out6, decoder_2_out0);
  T_Flip_Flop t_ff_82 (.clk(and_67_out), .T(and_67_out), .Q(out_4[5]));  // open: Qn, preset, reset, en
  and and_98 (and_98_out, decoder_1_out6, decoder_2_out1);
  and and_99 (and_99_out, decoder_1_out6, decoder_2_out2);
  T_Flip_Flop t_ff_83 (.clk(and_69_out), .T(and_69_out), .Q(out_5[5]));  // open: Qn, preset, reset, en
  T_Flip_Flop t_ff_84 (.clk(and_71_out), .T(and_71_out), .Q(out_6[5]));  // open: Qn, preset, reset, en
  and and_100 (and_100_out, decoder_1_out6, decoder_2_out3);
  and and_101 (and_101_out, decoder_1_out6, decoder_2_out4);
  T_Flip_Flop t_ff_85 (.clk(and_73_out), .T(and_73_out), .Q(out_7[5]));  // open: Qn, preset, reset, en
  T_Flip_Flop t_ff_86 (.clk(and_76_out), .T(and_76_out), .Q(out_8[5]));  // open: Qn, preset, reset, en
  and and_102 (and_102_out, decoder_1_out6, decoder_2_out5);
  T_Flip_Flop t_ff_87 (.clk(and_78_out), .T(and_78_out), .Q(out_9[5]));  // open: Qn, preset, reset, en
  and and_103 (and_103_out, decoder_1_out6, decoder_2_out6);
  and and_104 (and_104_out, decoder_1_out6, decoder_2_out7);
  T_Flip_Flop t_ff_88 (.clk(and_80_out), .T(and_80_out), .Q(out_10[5]));  // open: Qn, preset, reset, en
  and and_105 (and_105_out, decoder_1_out6, decoder_2_out8);
  T_Flip_Flop t_ff_89 (.clk(and_82_out), .T(and_82_out), .Q(out_11[5]));  // open: Qn, preset, reset, en
  T_Flip_Flop t_ff_90 (.clk(and_83_out), .T(and_83_out), .Q(out_12[5]));  // open: Qn, preset, reset, en
  and and_106 (and_106_out, decoder_1_out6, decoder_2_out9);
  T_Flip_Flop t_ff_91 (.clk(and_85_out), .T(and_85_out), .Q(out_13[5]));  // open: Qn, preset, reset, en
  and and_107 (and_107_out, decoder_1_out6, decoder_2_out10);
  and and_108 (and_108_out, decoder_1_out6, decoder_2_out11);
  T_Flip_Flop t_ff_92 (.clk(and_88_out), .T(and_88_out), .Q(out_14[5]));  // open: Qn, preset, reset, en
  T_Flip_Flop t_ff_93 (.clk(and_90_out), .T(and_90_out), .Q(out_15[5]));  // open: Qn, preset, reset, en
  and and_109 (and_109_out, decoder_1_out6, decoder_2_out12);
  T_Flip_Flop t_ff_94 (.clk(and_91_out), .T(and_91_out), .Q(out_16[5]));  // open: Qn, preset, reset, en
  and and_110 (and_110_out, decoder_1_out6, decoder_2_out13);
  T_Flip_Flop t_ff_95 (.clk(and_94_out), .T(and_94_out), .Q(out_17[5]));  // open: Qn, preset, reset, en
  and and_111 (and_111_out, decoder_1_out6, decoder_2_out14);
  and and_112 (and_112_out, decoder_1_out6, decoder_2_out15);
  T_Flip_Flop t_ff_96 (.clk(and_96_out), .T(and_96_out), .Q(out_18[5]));  // open: Qn, preset, reset, en
  T_Flip_Flop t_ff_97 (.clk(and_97_out), .T(and_97_out), .Q(out_3[6]));  // open: Qn, preset, reset, en
  and and_113 (and_113_out, decoder_1_out7, decoder_2_out0);
  T_Flip_Flop t_ff_98 (.clk(and_113_out), .T(and_113_out), .Q(out_3[7]));  // open: Qn, preset, reset, en
  T_Flip_Flop t_ff_99 (.clk(and_98_out), .T(and_98_out), .Q(out_4[6]));  // open: Qn, preset, reset, en
  and and_114 (and_114_out, decoder_1_out7, decoder_2_out1);
  T_Flip_Flop t_ff_100 (.clk(and_114_out), .T(and_114_out), .Q(out_4[7]));  // open: Qn, preset, reset, en
  and and_115 (and_115_out, decoder_1_out7, decoder_2_out2);
  T_Flip_Flop t_ff_101 (.clk(and_99_out), .T(and_99_out), .Q(out_5[6]));  // open: Qn, preset, reset, en
  T_Flip_Flop t_ff_102 (.clk(and_115_out), .T(and_115_out), .Q(out_5[7]));  // open: Qn, preset, reset, en
  T_Flip_Flop t_ff_103 (.clk(and_100_out), .T(and_100_out), .Q(out_6[6]));  // open: Qn, preset, reset, en
  and and_116 (and_116_out, decoder_1_out7, decoder_2_out3);
  T_Flip_Flop t_ff_104 (.clk(and_116_out), .T(and_116_out), .Q(out_6[7]));  // open: Qn, preset, reset, en
  and and_117 (and_117_out, decoder_1_out7, decoder_2_out4);
  T_Flip_Flop t_ff_105 (.clk(and_101_out), .T(and_101_out), .Q(out_7[6]));  // open: Qn, preset, reset, en
  T_Flip_Flop t_ff_106 (.clk(and_117_out), .T(and_117_out), .Q(out_7[7]));  // open: Qn, preset, reset, en
  T_Flip_Flop t_ff_107 (.clk(and_102_out), .T(and_102_out), .Q(out_8[6]));  // open: Qn, preset, reset, en
  T_Flip_Flop t_ff_108 (.clk(and_118_out), .T(and_118_out), .Q(out_8[7]));  // open: Qn, preset, reset, en
  and and_118 (and_118_out, decoder_1_out7, decoder_2_out5);
  T_Flip_Flop t_ff_109 (.clk(and_119_out), .T(and_119_out), .Q(out_9[7]));  // open: Qn, preset, reset, en
  T_Flip_Flop t_ff_110 (.clk(and_103_out), .T(and_103_out), .Q(out_9[6]));  // open: Qn, preset, reset, en
  and and_119 (and_119_out, decoder_1_out7, decoder_2_out6);
  and and_120 (and_120_out, decoder_1_out7, decoder_2_out7);
  T_Flip_Flop t_ff_111 (.clk(and_120_out), .T(and_120_out), .Q(out_10[7]));  // open: Qn, preset, reset, en
  T_Flip_Flop t_ff_112 (.clk(and_104_out), .T(and_104_out), .Q(out_10[6]));  // open: Qn, preset, reset, en
  and and_121 (and_121_out, decoder_1_out7, decoder_2_out8);
  T_Flip_Flop t_ff_113 (.clk(and_105_out), .T(and_105_out), .Q(out_11[6]));  // open: Qn, preset, reset, en
  T_Flip_Flop t_ff_114 (.clk(and_121_out), .T(and_121_out), .Q(out_11[7]));  // open: Qn, preset, reset, en
  T_Flip_Flop t_ff_115 (.clk(and_106_out), .T(and_106_out), .Q(out_12[6]));  // open: Qn, preset, reset, en
  T_Flip_Flop t_ff_116 (.clk(and_122_out), .T(and_122_out), .Q(out_12[7]));  // open: Qn, preset, reset, en
  and and_122 (and_122_out, decoder_1_out7, decoder_2_out9);
  and and_123 (and_123_out, decoder_1_out7, decoder_2_out10);
  T_Flip_Flop t_ff_117 (.clk(and_107_out), .T(and_107_out), .Q(out_13[6]));  // open: Qn, preset, reset, en
  T_Flip_Flop t_ff_118 (.clk(and_123_out), .T(and_123_out), .Q(out_13[7]));  // open: Qn, preset, reset, en
  and and_124 (and_124_out, decoder_1_out7, decoder_2_out11);
  T_Flip_Flop t_ff_119 (.clk(and_108_out), .T(and_108_out), .Q(out_14[6]));  // open: Qn, preset, reset, en
  T_Flip_Flop t_ff_120 (.clk(and_124_out), .T(and_124_out), .Q(out_14[7]));  // open: Qn, preset, reset, en
  T_Flip_Flop t_ff_121 (.clk(and_109_out), .T(and_109_out), .Q(out_15[6]));  // open: Qn, preset, reset, en
  T_Flip_Flop t_ff_122 (.clk(and_125_out), .T(and_125_out), .Q(out_15[7]));  // open: Qn, preset, reset, en
  and and_125 (and_125_out, decoder_1_out7, decoder_2_out12);
  and and_126 (and_126_out, decoder_1_out7, decoder_2_out13);
  T_Flip_Flop t_ff_123 (.clk(and_126_out), .T(and_126_out), .Q(out_16[7]));  // open: Qn, preset, reset, en
  T_Flip_Flop t_ff_124 (.clk(and_110_out), .T(and_110_out), .Q(out_16[6]));  // open: Qn, preset, reset, en
  T_Flip_Flop t_ff_125 (.clk(and_111_out), .T(and_111_out), .Q(out_17[6]));  // open: Qn, preset, reset, en
  T_Flip_Flop t_ff_126 (.clk(and_127_out), .T(and_127_out), .Q(out_17[7]));  // open: Qn, preset, reset, en
  and and_127 (and_127_out, decoder_1_out7, decoder_2_out14);
  T_Flip_Flop t_ff_127 (.clk(and_128_out), .T(and_128_out), .Q(out_18[7]));  // open: Qn, preset, reset, en
  and and_128 (and_128_out, decoder_1_out7, decoder_2_out15);
  T_Flip_Flop t_ff_128 (.clk(and_112_out), .T(and_112_out), .Q(out_18[6]));  // open: Qn, preset, reset, en
  and and_129 (and_129_out, decoder_1_out8, decoder_2_out0);
  T_Flip_Flop t_ff_129 (.clk(and_129_out), .T(and_129_out), .Q(out_3[8]));  // open: Qn, preset, reset, en
  and and_130 (and_130_out, decoder_1_out8, decoder_2_out1);
  T_Flip_Flop t_ff_130 (.clk(and_130_out), .T(and_130_out), .Q(out_4[8]));  // open: Qn, preset, reset, en
  T_Flip_Flop t_ff_131 (.clk(and_131_out), .T(and_131_out), .Q(out_5[8]));  // open: Qn, preset, reset, en
  and and_131 (and_131_out, decoder_1_out8, decoder_2_out2);
  T_Flip_Flop t_ff_132 (.clk(and_132_out), .T(and_132_out), .Q(out_6[8]));  // open: Qn, preset, reset, en
  and and_132 (and_132_out, decoder_1_out8, decoder_2_out3);
  and and_133 (and_133_out, decoder_1_out8, decoder_2_out4);
  T_Flip_Flop t_ff_133 (.clk(and_133_out), .T(and_133_out), .Q(out_7[8]));  // open: Qn, preset, reset, en
  T_Flip_Flop t_ff_134 (.clk(and_134_out), .T(and_134_out), .Q(out_8[8]));  // open: Qn, preset, reset, en
  and and_134 (and_134_out, decoder_1_out8, decoder_2_out5);
  T_Flip_Flop t_ff_135 (.clk(and_135_out), .T(and_135_out), .Q(out_9[8]));  // open: Qn, preset, reset, en
  and and_135 (and_135_out, decoder_1_out8, decoder_2_out6);
  T_Flip_Flop t_ff_136 (.clk(and_136_out), .T(and_136_out), .Q(out_10[8]));  // open: Qn, preset, reset, en
  and and_136 (and_136_out, decoder_1_out8, decoder_2_out7);
  and and_137 (and_137_out, decoder_1_out8, decoder_2_out8);
  T_Flip_Flop t_ff_137 (.clk(and_137_out), .T(and_137_out), .Q(out_11[8]));  // open: Qn, preset, reset, en
  T_Flip_Flop t_ff_138 (.clk(and_138_out), .T(and_138_out), .Q(out_12[8]));  // open: Qn, preset, reset, en
  and and_138 (and_138_out, decoder_1_out8, decoder_2_out9);
  T_Flip_Flop t_ff_139 (.clk(and_139_out), .T(and_139_out), .Q(out_13[8]));  // open: Qn, preset, reset, en
  and and_139 (and_139_out, decoder_1_out8, decoder_2_out10);
  T_Flip_Flop t_ff_140 (.clk(and_140_out), .T(and_140_out), .Q(out_14[8]));  // open: Qn, preset, reset, en
  and and_140 (and_140_out, decoder_1_out8, decoder_2_out11);
  and and_141 (and_141_out, decoder_1_out8, decoder_2_out12);
  T_Flip_Flop t_ff_141 (.clk(and_141_out), .T(and_141_out), .Q(out_15[8]));  // open: Qn, preset, reset, en
  and and_142 (and_142_out, decoder_1_out8, decoder_2_out13);
  T_Flip_Flop t_ff_142 (.clk(and_142_out), .T(and_142_out), .Q(out_16[8]));  // open: Qn, preset, reset, en
  and and_143 (and_143_out, decoder_1_out8, decoder_2_out14);
  T_Flip_Flop t_ff_143 (.clk(and_143_out), .T(and_143_out), .Q(out_17[8]));  // open: Qn, preset, reset, en
  and and_144 (and_144_out, decoder_1_out8, decoder_2_out15);
  T_Flip_Flop t_ff_144 (.clk(and_144_out), .T(and_144_out), .Q(out_18[8]));  // open: Qn, preset, reset, en
  and and_145 (and_145_out, decoder_1_out9, decoder_2_out0);
  T_Flip_Flop t_ff_145 (.clk(and_145_out), .T(and_145_out), .Q(out_3[9]));  // open: Qn, preset, reset, en
  and and_146 (and_146_out, decoder_1_out9, decoder_2_out1);
  T_Flip_Flop t_ff_146 (.clk(and_146_out), .T(and_146_out), .Q(out_4[9]));  // open: Qn, preset, reset, en
  and and_147 (and_147_out, decoder_1_out9, decoder_2_out2);
  T_Flip_Flop t_ff_147 (.clk(and_147_out), .T(and_147_out), .Q(out_5[9]));  // open: Qn, preset, reset, en
  and and_148 (and_148_out, decoder_1_out9, decoder_2_out3);
  T_Flip_Flop t_ff_148 (.clk(and_148_out), .T(and_148_out), .Q(out_6[9]));  // open: Qn, preset, reset, en
  T_Flip_Flop t_ff_149 (.clk(and_149_out), .T(and_149_out), .Q(out_7[9]));  // open: Qn, preset, reset, en
  and and_149 (and_149_out, decoder_1_out9, decoder_2_out4);
  and and_150 (and_150_out, decoder_1_out9, decoder_2_out5);
  T_Flip_Flop t_ff_150 (.clk(and_150_out), .T(and_150_out), .Q(out_8[9]));  // open: Qn, preset, reset, en
  and and_151 (and_151_out, decoder_1_out9, decoder_2_out6);
  T_Flip_Flop t_ff_151 (.clk(and_151_out), .T(and_151_out), .Q(out_9[9]));  // open: Qn, preset, reset, en
  T_Flip_Flop t_ff_152 (.clk(and_152_out), .T(and_152_out), .Q(out_10[9]));  // open: Qn, preset, reset, en
  and and_152 (and_152_out, decoder_1_out9, decoder_2_out7);
  and and_153 (and_153_out, decoder_1_out9, decoder_2_out8);
  T_Flip_Flop t_ff_153 (.clk(and_153_out), .T(and_153_out), .Q(out_11[9]));  // open: Qn, preset, reset, en
  T_Flip_Flop t_ff_154 (.clk(and_154_out), .T(and_154_out), .Q(out_12[9]));  // open: Qn, preset, reset, en
  and and_154 (and_154_out, decoder_1_out9, decoder_2_out9);
  and and_155 (and_155_out, decoder_1_out9, decoder_2_out10);
  T_Flip_Flop t_ff_155 (.clk(and_155_out), .T(and_155_out), .Q(out_13[9]));  // open: Qn, preset, reset, en
  T_Flip_Flop t_ff_156 (.clk(and_156_out), .T(and_156_out), .Q(out_14[9]));  // open: Qn, preset, reset, en
  and and_156 (and_156_out, decoder_1_out9, decoder_2_out11);
  and and_157 (and_157_out, decoder_1_out9, decoder_2_out12);
  T_Flip_Flop t_ff_157 (.clk(and_157_out), .T(and_157_out), .Q(out_15[9]));  // open: Qn, preset, reset, en
  T_Flip_Flop t_ff_158 (.clk(and_158_out), .T(and_158_out), .Q(out_16[9]));  // open: Qn, preset, reset, en
  and and_158 (and_158_out, decoder_1_out9, decoder_2_out13);
  and and_159 (and_159_out, decoder_1_out9, decoder_2_out14);
  T_Flip_Flop t_ff_159 (.clk(and_159_out), .T(and_159_out), .Q(out_17[9]));  // open: Qn, preset, reset, en
  and and_160 (and_160_out, decoder_1_out9, decoder_2_out15);
  T_Flip_Flop t_ff_160 (.clk(and_160_out), .T(and_160_out), .Q(out_18[9]));  // open: Qn, preset, reset, en
  and and_161 (and_161_out, decoder_1_out10, decoder_2_out0);
  T_Flip_Flop t_ff_161 (.clk(and_161_out), .T(and_161_out), .Q(out_3[10]));  // open: Qn, preset, reset, en
  T_Flip_Flop t_ff_162 (.clk(and_162_out), .T(and_162_out), .Q(out_4[10]));  // open: Qn, preset, reset, en
  and and_162 (and_162_out, decoder_1_out10, decoder_2_out1);
  T_Flip_Flop t_ff_163 (.clk(and_163_out), .T(and_163_out), .Q(out_5[10]));  // open: Qn, preset, reset, en
  and and_163 (and_163_out, decoder_1_out10, decoder_2_out2);
  and and_164 (and_164_out, decoder_1_out10, decoder_2_out3);
  T_Flip_Flop t_ff_164 (.clk(and_164_out), .T(and_164_out), .Q(out_6[10]));  // open: Qn, preset, reset, en
  and and_165 (and_165_out, decoder_1_out10, decoder_2_out4);
  T_Flip_Flop t_ff_165 (.clk(and_165_out), .T(and_165_out), .Q(out_7[10]));  // open: Qn, preset, reset, en
  and and_166 (and_166_out, decoder_1_out10, decoder_2_out5);
  T_Flip_Flop t_ff_166 (.clk(and_166_out), .T(and_166_out), .Q(out_8[10]));  // open: Qn, preset, reset, en
  T_Flip_Flop t_ff_167 (.clk(and_167_out), .T(and_167_out), .Q(out_9[10]));  // open: Qn, preset, reset, en
  and and_167 (and_167_out, decoder_1_out10, decoder_2_out6);
  T_Flip_Flop t_ff_168 (.clk(and_168_out), .T(and_168_out), .Q(out_10[10]));  // open: Qn, preset, reset, en
  and and_168 (and_168_out, decoder_1_out10, decoder_2_out7);
  T_Flip_Flop t_ff_169 (.clk(and_169_out), .T(and_169_out), .Q(out_11[10]));  // open: Qn, preset, reset, en
  and and_169 (and_169_out, decoder_1_out10, decoder_2_out8);
  T_Flip_Flop t_ff_170 (.clk(and_170_out), .T(and_170_out), .Q(out_12[10]));  // open: Qn, preset, reset, en
  and and_170 (and_170_out, decoder_1_out10, decoder_2_out9);
  and and_171 (and_171_out, decoder_1_out10, decoder_2_out10);
  T_Flip_Flop t_ff_171 (.clk(and_171_out), .T(and_171_out), .Q(out_13[10]));  // open: Qn, preset, reset, en
  T_Flip_Flop t_ff_172 (.clk(and_172_out), .T(and_172_out), .Q(out_14[10]));  // open: Qn, preset, reset, en
  and and_172 (and_172_out, decoder_1_out10, decoder_2_out11);
  T_Flip_Flop t_ff_173 (.clk(and_173_out), .T(and_173_out), .Q(out_15[10]));  // open: Qn, preset, reset, en
  and and_173 (and_173_out, decoder_1_out10, decoder_2_out12);
  T_Flip_Flop t_ff_174 (.clk(and_174_out), .T(and_174_out), .Q(out_16[10]));  // open: Qn, preset, reset, en
  and and_174 (and_174_out, decoder_1_out10, decoder_2_out13);
  T_Flip_Flop t_ff_175 (.clk(and_175_out), .T(and_175_out), .Q(out_17[10]));  // open: Qn, preset, reset, en
  and and_175 (and_175_out, decoder_1_out10, decoder_2_out14);
  and and_176 (and_176_out, decoder_1_out10, decoder_2_out15);
  T_Flip_Flop t_ff_176 (.clk(and_176_out), .T(and_176_out), .Q(out_18[10]));  // open: Qn, preset, reset, en
  and and_177 (and_177_out, decoder_1_out11, decoder_2_out0);
  T_Flip_Flop t_ff_177 (.clk(and_177_out), .T(and_177_out), .Q(out_3[11]));  // open: Qn, preset, reset, en
  T_Flip_Flop t_ff_178 (.clk(and_178_out), .T(and_178_out), .Q(out_4[11]));  // open: Qn, preset, reset, en
  and and_178 (and_178_out, decoder_1_out11, decoder_2_out1);
  T_Flip_Flop t_ff_179 (.clk(and_179_out), .T(and_179_out), .Q(out_5[11]));  // open: Qn, preset, reset, en
  and and_179 (and_179_out, decoder_1_out11, decoder_2_out2);
  and and_180 (and_180_out, decoder_1_out11, decoder_2_out3);
  T_Flip_Flop t_ff_180 (.clk(and_180_out), .T(and_180_out), .Q(out_6[11]));  // open: Qn, preset, reset, en
  T_Flip_Flop t_ff_181 (.clk(and_181_out), .T(and_181_out), .Q(out_7[11]));  // open: Qn, preset, reset, en
  and and_181 (and_181_out, decoder_1_out11, decoder_2_out4);
  T_Flip_Flop t_ff_182 (.clk(and_182_out), .T(and_182_out), .Q(out_8[11]));  // open: Qn, preset, reset, en
  and and_182 (and_182_out, decoder_1_out11, decoder_2_out5);
  and and_183 (and_183_out, decoder_1_out11, decoder_2_out6);
  T_Flip_Flop t_ff_183 (.clk(and_183_out), .T(and_183_out), .Q(out_9[11]));  // open: Qn, preset, reset, en
  and and_184 (and_184_out, decoder_1_out11, decoder_2_out7);
  T_Flip_Flop t_ff_184 (.clk(and_184_out), .T(and_184_out), .Q(out_10[11]));  // open: Qn, preset, reset, en
  T_Flip_Flop t_ff_185 (.clk(and_185_out), .T(and_185_out), .Q(out_11[11]));  // open: Qn, preset, reset, en
  and and_185 (and_185_out, decoder_1_out11, decoder_2_out8);
  and and_186 (and_186_out, decoder_1_out11, decoder_2_out9);
  T_Flip_Flop t_ff_186 (.clk(and_186_out), .T(and_186_out), .Q(out_12[11]));  // open: Qn, preset, reset, en
  T_Flip_Flop t_ff_187 (.clk(and_187_out), .T(and_187_out), .Q(out_13[11]));  // open: Qn, preset, reset, en
  and and_187 (and_187_out, decoder_1_out11, decoder_2_out10);
  and and_188 (and_188_out, decoder_1_out11, decoder_2_out11);
  T_Flip_Flop t_ff_188 (.clk(and_188_out), .T(and_188_out), .Q(out_14[11]));  // open: Qn, preset, reset, en
  and and_189 (and_189_out, decoder_1_out11, decoder_2_out12);
  T_Flip_Flop t_ff_189 (.clk(and_189_out), .T(and_189_out), .Q(out_15[11]));  // open: Qn, preset, reset, en
  T_Flip_Flop t_ff_190 (.clk(and_190_out), .T(and_190_out), .Q(out_16[11]));  // open: Qn, preset, reset, en
  and and_190 (and_190_out, decoder_1_out11, decoder_2_out13);
  T_Flip_Flop t_ff_191 (.clk(and_191_out), .T(and_191_out), .Q(out_17[11]));  // open: Qn, preset, reset, en
  and and_191 (and_191_out, decoder_1_out11, decoder_2_out14);
  T_Flip_Flop t_ff_192 (.clk(and_192_out), .T(and_192_out), .Q(out_18[11]));  // open: Qn, preset, reset, en
  and and_192 (and_192_out, decoder_1_out11, decoder_2_out15);
  and and_193 (and_193_out, decoder_1_out13, decoder_2_out0);
  T_Flip_Flop t_ff_193 (.clk(and_194_out), .T(and_194_out), .Q(out_3[12]));  // open: Qn, preset, reset, en
  and and_194 (and_194_out, decoder_1_out12, decoder_2_out0);
  and and_195 (and_195_out, decoder_1_out12, decoder_2_out1);
  T_Flip_Flop t_ff_194 (.clk(and_195_out), .T(and_195_out), .Q(out_4[12]));  // open: Qn, preset, reset, en
  and and_196 (and_196_out, decoder_1_out13, decoder_2_out1);
  and and_197 (and_197_out, decoder_1_out12, decoder_2_out2);
  T_Flip_Flop t_ff_195 (.clk(and_197_out), .T(and_197_out), .Q(out_5[12]));  // open: Qn, preset, reset, en
  and and_198 (and_198_out, decoder_1_out13, decoder_2_out2);
  and and_199 (and_199_out, decoder_1_out12, decoder_2_out3);
  and and_200 (and_200_out, decoder_1_out13, decoder_2_out3);
  T_Flip_Flop t_ff_196 (.clk(and_199_out), .T(and_199_out), .Q(out_6[12]));  // open: Qn, preset, reset, en
  and and_201 (and_201_out, decoder_1_out13, decoder_2_out4);
  T_Flip_Flop t_ff_197 (.clk(and_202_out), .T(and_202_out), .Q(out_7[12]));  // open: Qn, preset, reset, en
  and and_202 (and_202_out, decoder_1_out12, decoder_2_out4);
  and and_203 (and_203_out, decoder_1_out13, decoder_2_out5);
  and and_204 (and_204_out, decoder_1_out12, decoder_2_out5);
  T_Flip_Flop t_ff_198 (.clk(and_204_out), .T(and_204_out), .Q(out_8[12]));  // open: Qn, preset, reset, en
  and and_205 (and_205_out, decoder_1_out13, decoder_2_out6);
  and and_206 (and_206_out, decoder_1_out12, decoder_2_out6);
  T_Flip_Flop t_ff_199 (.clk(and_206_out), .T(and_206_out), .Q(out_9[12]));  // open: Qn, preset, reset, en
  and and_207 (and_207_out, decoder_1_out12, decoder_2_out7);
  T_Flip_Flop t_ff_200 (.clk(and_207_out), .T(and_207_out), .Q(out_10[12]));  // open: Qn, preset, reset, en
  and and_208 (and_208_out, decoder_1_out13, decoder_2_out7);
  T_Flip_Flop t_ff_201 (.clk(and_209_out), .T(and_209_out), .Q(out_11[12]));  // open: Qn, preset, reset, en
  and and_209 (and_209_out, decoder_1_out12, decoder_2_out8);
  and and_210 (and_210_out, decoder_1_out13, decoder_2_out8);
  and and_211 (and_211_out, decoder_1_out13, decoder_2_out9);
  and and_212 (and_212_out, decoder_1_out12, decoder_2_out9);
  T_Flip_Flop t_ff_202 (.clk(and_212_out), .T(and_212_out), .Q(out_12[12]));  // open: Qn, preset, reset, en
  T_Flip_Flop t_ff_203 (.clk(and_214_out), .T(and_214_out), .Q(out_13[12]));  // open: Qn, preset, reset, en
  and and_213 (and_213_out, decoder_1_out13, decoder_2_out10);
  and and_214 (and_214_out, decoder_1_out12, decoder_2_out10);
  and and_215 (and_215_out, decoder_1_out12, decoder_2_out11);
  T_Flip_Flop t_ff_204 (.clk(and_215_out), .T(and_215_out), .Q(out_14[12]));  // open: Qn, preset, reset, en
  and and_216 (and_216_out, decoder_1_out13, decoder_2_out11);
  and and_217 (and_217_out, decoder_1_out13, decoder_2_out12);
  T_Flip_Flop t_ff_205 (.clk(and_218_out), .T(and_218_out), .Q(out_15[12]));  // open: Qn, preset, reset, en
  and and_218 (and_218_out, decoder_1_out12, decoder_2_out12);
  and and_219 (and_219_out, decoder_1_out13, decoder_2_out13);
  T_Flip_Flop t_ff_206 (.clk(and_220_out), .T(and_220_out), .Q(out_16[12]));  // open: Qn, preset, reset, en
  and and_220 (and_220_out, decoder_1_out12, decoder_2_out13);
  and and_221 (and_221_out, decoder_1_out13, decoder_2_out14);
  T_Flip_Flop t_ff_207 (.clk(and_222_out), .T(and_222_out), .Q(out_17[12]));  // open: Qn, preset, reset, en
  and and_222 (and_222_out, decoder_1_out12, decoder_2_out14);
  T_Flip_Flop t_ff_208 (.clk(and_223_out), .T(and_223_out), .Q(out_18[12]));  // open: Qn, preset, reset, en
  and and_223 (and_223_out, decoder_1_out12, decoder_2_out15);
  and and_224 (and_224_out, decoder_1_out13, decoder_2_out15);
  and and_225 (and_225_out, decoder_1_out14, decoder_2_out0);
  T_Flip_Flop t_ff_209 (.clk(and_193_out), .T(and_193_out), .Q(out_3[13]));  // open: Qn, preset, reset, en
  T_Flip_Flop t_ff_210 (.clk(and_196_out), .T(and_196_out), .Q(out_4[13]));  // open: Qn, preset, reset, en
  and and_226 (and_226_out, decoder_1_out14, decoder_2_out1);
  and and_227 (and_227_out, decoder_1_out14, decoder_2_out2);
  T_Flip_Flop t_ff_211 (.clk(and_198_out), .T(and_198_out), .Q(out_5[13]));  // open: Qn, preset, reset, en
  and and_228 (and_228_out, decoder_1_out14, decoder_2_out3);
  T_Flip_Flop t_ff_212 (.clk(and_200_out), .T(and_200_out), .Q(out_6[13]));  // open: Qn, preset, reset, en
  T_Flip_Flop t_ff_213 (.clk(and_201_out), .T(and_201_out), .Q(out_7[13]));  // open: Qn, preset, reset, en
  and and_229 (and_229_out, decoder_1_out14, decoder_2_out4);
  and and_230 (and_230_out, decoder_1_out14, decoder_2_out5);
  T_Flip_Flop t_ff_214 (.clk(and_203_out), .T(and_203_out), .Q(out_8[13]));  // open: Qn, preset, reset, en
  and and_231 (and_231_out, decoder_1_out14, decoder_2_out6);
  T_Flip_Flop t_ff_215 (.clk(and_205_out), .T(and_205_out), .Q(out_9[13]));  // open: Qn, preset, reset, en
  T_Flip_Flop t_ff_216 (.clk(and_208_out), .T(and_208_out), .Q(out_10[13]));  // open: Qn, preset, reset, en
  and and_232 (and_232_out, decoder_1_out14, decoder_2_out7);
  and and_233 (and_233_out, decoder_1_out14, decoder_2_out8);
  T_Flip_Flop t_ff_217 (.clk(and_210_out), .T(and_210_out), .Q(out_11[13]));  // open: Qn, preset, reset, en
  T_Flip_Flop t_ff_218 (.clk(and_211_out), .T(and_211_out), .Q(out_12[13]));  // open: Qn, preset, reset, en
  and and_234 (and_234_out, decoder_1_out14, decoder_2_out9);
  T_Flip_Flop t_ff_219 (.clk(and_213_out), .T(and_213_out), .Q(out_13[13]));  // open: Qn, preset, reset, en
  and and_235 (and_235_out, decoder_1_out14, decoder_2_out10);
  and and_236 (and_236_out, decoder_1_out14, decoder_2_out11);
  T_Flip_Flop t_ff_220 (.clk(and_216_out), .T(and_216_out), .Q(out_14[13]));  // open: Qn, preset, reset, en
  T_Flip_Flop t_ff_221 (.clk(and_217_out), .T(and_217_out), .Q(out_15[13]));  // open: Qn, preset, reset, en
  and and_237 (and_237_out, decoder_1_out14, decoder_2_out12);
  and and_238 (and_238_out, decoder_1_out14, decoder_2_out13);
  T_Flip_Flop t_ff_222 (.clk(and_219_out), .T(and_219_out), .Q(out_16[13]));  // open: Qn, preset, reset, en
  T_Flip_Flop t_ff_223 (.clk(and_221_out), .T(and_221_out), .Q(out_17[13]));  // open: Qn, preset, reset, en
  and and_239 (and_239_out, decoder_1_out14, decoder_2_out14);
  and and_240 (and_240_out, decoder_1_out14, decoder_2_out15);
  T_Flip_Flop t_ff_224 (.clk(and_224_out), .T(and_224_out), .Q(out_18[13]));  // open: Qn, preset, reset, en
  and and_241 (and_241_out, decoder_1_out15, decoder_2_out0);
  T_Flip_Flop t_ff_225 (.clk(and_225_out), .T(and_225_out), .Q(out_3[14]));  // open: Qn, preset, reset, en
  T_Flip_Flop t_ff_226 (.clk(and_241_out), .T(and_241_out), .Q(out_3[15]));  // open: Qn, preset, reset, en
  and and_242 (and_242_out, decoder_1_out15, decoder_2_out1);
  T_Flip_Flop t_ff_227 (.clk(and_226_out), .T(and_226_out), .Q(out_4[14]));  // open: Qn, preset, reset, en
  T_Flip_Flop t_ff_228 (.clk(and_242_out), .T(and_242_out), .Q(out_4[15]));  // open: Qn, preset, reset, en
  T_Flip_Flop t_ff_229 (.clk(and_227_out), .T(and_227_out), .Q(out_5[14]));  // open: Qn, preset, reset, en
  and and_243 (and_243_out, decoder_1_out15, decoder_2_out2);
  T_Flip_Flop t_ff_230 (.clk(and_243_out), .T(and_243_out), .Q(out_5[15]));  // open: Qn, preset, reset, en
  T_Flip_Flop t_ff_231 (.clk(and_244_out), .T(and_244_out), .Q(out_6[15]));  // open: Qn, preset, reset, en
  T_Flip_Flop t_ff_232 (.clk(and_228_out), .T(and_228_out), .Q(out_6[14]));  // open: Qn, preset, reset, en
  and and_244 (and_244_out, decoder_1_out15, decoder_2_out3);
  and and_245 (and_245_out, decoder_1_out15, decoder_2_out4);
  T_Flip_Flop t_ff_233 (.clk(and_245_out), .T(and_245_out), .Q(out_7[15]));  // open: Qn, preset, reset, en
  T_Flip_Flop t_ff_234 (.clk(and_229_out), .T(and_229_out), .Q(out_7[14]));  // open: Qn, preset, reset, en
  T_Flip_Flop t_ff_235 (.clk(and_246_out), .T(and_246_out), .Q(out_8[15]));  // open: Qn, preset, reset, en
  and and_246 (and_246_out, decoder_1_out15, decoder_2_out5);
  T_Flip_Flop t_ff_236 (.clk(and_230_out), .T(and_230_out), .Q(out_8[14]));  // open: Qn, preset, reset, en
  T_Flip_Flop t_ff_237 (.clk(and_247_out), .T(and_247_out), .Q(out_9[15]));  // open: Qn, preset, reset, en
  T_Flip_Flop t_ff_238 (.clk(and_231_out), .T(and_231_out), .Q(out_9[14]));  // open: Qn, preset, reset, en
  and and_247 (and_247_out, decoder_1_out15, decoder_2_out6);
  T_Flip_Flop t_ff_239 (.clk(and_232_out), .T(and_232_out), .Q(out_10[14]));  // open: Qn, preset, reset, en
  and and_248 (and_248_out, decoder_1_out15, decoder_2_out7);
  T_Flip_Flop t_ff_240 (.clk(and_248_out), .T(and_248_out), .Q(out_10[15]));  // open: Qn, preset, reset, en
  T_Flip_Flop t_ff_241 (.clk(and_249_out), .T(and_249_out), .Q(out_11[15]));  // open: Qn, preset, reset, en
  and and_249 (and_249_out, decoder_1_out15, decoder_2_out8);
  T_Flip_Flop t_ff_242 (.clk(and_233_out), .T(and_233_out), .Q(out_11[14]));  // open: Qn, preset, reset, en
  and and_250 (and_250_out, decoder_1_out15, decoder_2_out9);
  T_Flip_Flop t_ff_243 (.clk(and_234_out), .T(and_234_out), .Q(out_12[14]));  // open: Qn, preset, reset, en
  T_Flip_Flop t_ff_244 (.clk(and_250_out), .T(and_250_out), .Q(out_12[15]));  // open: Qn, preset, reset, en
  T_Flip_Flop t_ff_245 (.clk(and_251_out), .T(and_251_out), .Q(out_13[15]));  // open: Qn, preset, reset, en
  and and_251 (and_251_out, decoder_1_out15, decoder_2_out10);
  T_Flip_Flop t_ff_246 (.clk(and_235_out), .T(and_235_out), .Q(out_13[14]));  // open: Qn, preset, reset, en
  T_Flip_Flop t_ff_247 (.clk(and_236_out), .T(and_236_out), .Q(out_14[14]));  // open: Qn, preset, reset, en
  T_Flip_Flop t_ff_248 (.clk(and_252_out), .T(and_252_out), .Q(out_14[15]));  // open: Qn, preset, reset, en
  and and_252 (and_252_out, decoder_1_out15, decoder_2_out11);
  and and_253 (and_253_out, decoder_1_out15, decoder_2_out12);
  T_Flip_Flop t_ff_249 (.clk(and_237_out), .T(and_237_out), .Q(out_15[14]));  // open: Qn, preset, reset, en
  T_Flip_Flop t_ff_250 (.clk(and_253_out), .T(and_253_out), .Q(out_15[15]));  // open: Qn, preset, reset, en
  T_Flip_Flop t_ff_251 (.clk(and_238_out), .T(and_238_out), .Q(out_16[14]));  // open: Qn, preset, reset, en
  and and_254 (and_254_out, decoder_1_out15, decoder_2_out13);
  T_Flip_Flop t_ff_252 (.clk(and_254_out), .T(and_254_out), .Q(out_16[15]));  // open: Qn, preset, reset, en
  T_Flip_Flop t_ff_253 (.clk(and_255_out), .T(and_255_out), .Q(out_17[15]));  // open: Qn, preset, reset, en
  T_Flip_Flop t_ff_254 (.clk(and_239_out), .T(and_239_out), .Q(out_17[14]));  // open: Qn, preset, reset, en
  and and_255 (and_255_out, decoder_1_out15, decoder_2_out14);
  T_Flip_Flop t_ff_255 (.clk(and_256_out), .T(and_256_out), .Q(out_18[15]));  // open: Qn, preset, reset, en
  and and_256 (and_256_out, decoder_1_out15, decoder_2_out15);
  T_Flip_Flop t_ff_256 (.clk(and_240_out), .T(and_240_out), .Q(out_18[14]));  // open: Qn, preset, reset, en
endmodule
